// Logisim project 1_基本逻辑门电路.circ as structural Verilog: 1 circuit, main circuit main
module main (
  input  \与门 ,
  input  in_2,
  input  \或门 ,
  input  in_4,
  input  \非门 ,
  input  \与非门 ,
  input  in_7,
  input  \或非门 ,
  input  in_9,
  input  \异或门 ,
  input  in_11,
  input  \同或门 ,
  input  in_13,
  output out_14,
  output out_15,
  output out_16,
  output out_17,
  output out_18,
  output out_19,
  output out_20
);

  wire and_2_out, and_4_out, nand_1_out, nand_2_out, or_2_out, or_3_out, or_4_out;

  and and_1 (out_14, \与门 , in_2);
  or or_1 (out_15, \或门 , in_4);
  not not_1 (out_16, \非门 );
  and and_2 (and_2_out, \与非门 , in_7);
  or or_2 (or_2_out, \或非门 , in_9);
  or or_3 (or_3_out, \异或门 , in_11);
  nand nand_1 (nand_1_out, \异或门 , in_11);
  or or_4 (or_4_out, \同或门 , in_13);
  nand nand_2 (nand_2_out, \同或门 , in_13);
  not not_2 (out_17, and_2_out);
  not not_3 (out_18, or_2_out);
  and and_3 (out_19, or_3_out, nand_1_out);
  and and_4 (and_4_out, or_4_out, nand_2_out);
  not not_4 (out_20, and_4_out);
  // NAND_Gate nand_3 is placed but not wired
  // NOR_Gate nor_1 is placed but not wired
  // XOR_Gate xor_1 is placed but not wired
  // XNOR_Gate xnor_1 is placed but not wired
endmodule
