// Logisim project 2_半加器_全加器_八位加法器.circ as structural Verilog: 4 circuits, main circuit main
module main (
);

  \半加器  \u_半加器  ();  // open: Carry, Sum, A, B
  \全加器  \u_全加器  ();  // open: Carry, Sum, Cin, A, B
  \八位加法器  \u_八位加法器_1  ();  // open: A1, A2, A3, A4, A5, A6, A7, A8, B1, B2, B3, B4, B5, B6, B7, B8, in_1, C, A8_2, A7_2, A6_2, A5_2, A4_2, A3_2, A2_2, A1_2
endmodule

module \半加器  (
  input  A,
  input  B,
  output Carry,
  output Sum
);

  and and_1 (Carry, A, B);
  xor xor_1 (Sum, A, B);
endmodule

module \全加器  (
  input  Cin,
  input  A,
  input  B,
  output Carry,
  output Sum
);

  wire and_1_out, and_2_out, xor_3_out;

  xor xor_1 (Carry, and_2_out, and_1_out);
  and and_1 (and_1_out, Cin, xor_3_out);
  and and_2 (and_2_out, A, B);
  xor xor_2 (Sum, Cin, xor_3_out);
  xor xor_3 (xor_3_out, A, B);
endmodule

module \八位加法器  (
  input  in_1,
  input  A1,
  input  A2,
  input  A3,
  input  A4,
  input  A5,
  input  A6,
  input  A7,
  input  A8,
  input  B1,
  input  B2,
  input  B3,
  input  B4,
  input  B5,
  input  B6,
  input  B7,
  input  B8,
  output C,
  output A8_2,
  output A7_2,
  output A6_2,
  output A5_2,
  output A4_2,
  output A3_2,
  output A2_2,
  output A1_2
);

  wire \全加器_1_carry , \全加器_3_carry , \全加器_4_carry , \全加器_5_carry , \全加器_6_carry , \全加器_7_carry ,
       \全加器_8_carry ;

  \全加器  \u_全加器_1  (.Carry(\全加器_1_carry ), .Sum(A7_2), .Cin(\全加器_3_carry ), .A(A7), .B(B7));
  \全加器  \u_全加器_2  (.Carry(C), .Sum(A8_2), .Cin(\全加器_1_carry ), .A(A8), .B(B8));
  \全加器  \u_全加器_3  (.Carry(\全加器_3_carry ), .Sum(A6_2), .Cin(\全加器_4_carry ), .A(A6), .B(B6));
  \全加器  \u_全加器_4  (.Carry(\全加器_4_carry ), .Sum(A5_2), .Cin(\全加器_5_carry ), .A(A5), .B(B5));
  \全加器  \u_全加器_5  (.Carry(\全加器_5_carry ), .Sum(A4_2), .Cin(\全加器_6_carry ), .A(A4), .B(B4));
  \全加器  \u_全加器_6  (.Carry(\全加器_6_carry ), .Sum(A3_2), .Cin(\全加器_7_carry ), .A(A3), .B(B3));
  \全加器  \u_全加器_7  (.Carry(\全加器_7_carry ), .Sum(A2_2), .Cin(\全加器_8_carry ), .A(A2), .B(B2));
  \全加器  \u_全加器_8  (.Carry(\全加器_8_carry ), .Sum(A1_2), .Cin(in_1), .A(A1), .B(B1));
endmodule
