// Logisim project ALU.circ as structural Verilog: 14 circuits, main circuit main
module main (
  input  [7:0] in_1,
  input  in_2,
  output [7:0] out_3,
  output out_4
);

  wire \右移位器8位_1_shift_out ;
  wire [7:0] \右移位器8位_1_right_shift_out ;

  \右移位器8位  \u_右移位器8位_1  (
    .right_shift_in(in_1), .shift_in(in_2), .shift_out(\右移位器8位_1_shift_out ),
    .right_shift_out(\右移位器8位_1_right_shift_out ));
  \右移位器8位  \u_右移位器8位_2  (
    .right_shift_in(\右移位器8位_1_right_shift_out ), .shift_in(\右移位器8位_1_shift_out ), .shift_out(out_4),
    .right_shift_out(out_3));
endmodule

module \右移位器8位  (
  input  [7:0] right_shift_in,
  input  shift_in,
  output shift_out,
  output [7:0] right_shift_out
);


  assign right_shift_out = {shift_in, right_shift_in[7:1]};
  assign shift_out = right_shift_in[0];
endmodule

module \左移位器8位  (
  input  shift_in,
  input  [7:0] left_shift_in,
  output [7:0] left_shift_out,
  output shift_out
);


  assign left_shift_out = {left_shift_in[6:0], shift_in};
  assign shift_out = left_shift_in[7];
endmodule

module \与门8位  (
  input  [7:0] A,
  input  [7:0] B,
  output [7:0] OUT
);

  assign OUT = A & B;  // AND_Gate and_1, 8 bits wide
endmodule

module \或门8位  (
  input  [7:0] A,
  input  [7:0] B,
  output [7:0] OUT
);

  assign OUT = A | B;  // OR_Gate or_1, 8 bits wide
endmodule

module \非门8位  (
  input  [7:0] IN,
  output [7:0] OUT
);

  assign OUT = ~IN;  // NOT_Gate not_1, 8 bits wide
endmodule

module \半加器  (
  input  A,
  input  B,
  output S,
  output C
);

  xor xor_1 (S, A, B);
  and and_1 (C, A, B);
endmodule

module \全加器  (
  input  A,
  input  B,
  input  C_IN,
  output S,
  output C_OUT
);

  wire and_1_out, and_2_out, xor_1_out;

  xor xor_1 (xor_1_out, A, B);
  and and_1 (and_1_out, A, B);
  xor xor_2 (S, xor_1_out, C_IN);
  and and_2 (and_2_out, xor_1_out, C_IN);
  or or_1 (C_OUT, and_2_out, and_1_out);
endmodule

module \加法器8位  (
  input  [7:0] A,
  input  C_IN,
  input  [7:0] B,
  output [7:0] S,
  output C_OUT
);

  wire \全加器_1_c_out , \全加器_2_c_out , \全加器_3_c_out , \全加器_4_c_out , \全加器_5_c_out , \全加器_6_c_out ,
       \全加器_7_c_out ;

  \全加器  \u_全加器_1  (.A(A[0]), .B(B[0]), .C_IN(C_IN), .S(S[0]), .C_OUT(\全加器_1_c_out ));
  \全加器  \u_全加器_2  (.A(A[1]), .B(B[1]), .C_IN(\全加器_1_c_out ), .S(S[1]), .C_OUT(\全加器_2_c_out ));
  \全加器  \u_全加器_3  (.A(A[2]), .B(B[2]), .C_IN(\全加器_2_c_out ), .S(S[2]), .C_OUT(\全加器_3_c_out ));
  \全加器  \u_全加器_4  (.A(A[3]), .B(B[3]), .C_IN(\全加器_3_c_out ), .S(S[3]), .C_OUT(\全加器_4_c_out ));
  \全加器  \u_全加器_5  (.A(A[4]), .B(B[4]), .C_IN(\全加器_4_c_out ), .S(S[4]), .C_OUT(\全加器_5_c_out ));
  \全加器  \u_全加器_6  (.A(A[5]), .B(B[5]), .C_IN(\全加器_5_c_out ), .S(S[5]), .C_OUT(\全加器_6_c_out ));
  \全加器  \u_全加器_7  (.A(A[6]), .B(B[6]), .C_IN(\全加器_6_c_out ), .S(S[6]), .C_OUT(\全加器_7_c_out ));
  \全加器  \u_全加器_8  (.A(A[7]), .B(B[7]), .C_IN(\全加器_7_c_out ), .S(S[7]), .C_OUT(C_OUT));
endmodule

module \比较器  (
  input  \上一个与门传下来的默认为1 ,
  input  \上一位或门传下来的默认为0 ,
  input  A,
  input  B,
  output \不相同 ,
  output \上一位和当前位都相同 ,
  output \说明A比B大 
);

  wire and_2_out, not_1_out;

  xor xor_1 (\不相同 , A, B);
  not not_1 (not_1_out, \不相同 );
  and and_1 (\上一位和当前位都相同 , not_1_out, \上一个与门传下来的默认为1 );
  and and_2 (and_2_out, \上一个与门传下来的默认为1 , A, \不相同 );
  or or_1 (\说明A比B大 , and_2_out, \上一位或门传下来的默认为0 );

  // Notes on the sheet:
  //   从高位到低位比较
  //   不相同
  //   相同
endmodule

module \比较器8位  (
  input  [7:0] A,
  input  [7:0] B,
  output [7:0] \不相同的位数 ,
  output \A大于B ,
  output \相同 
);

  wire \比较器_1_上一位和当前位都相同 , \比较器_1_说明a比b大 , \比较器_2_上一位和当前位都相同 , \比较器_2_说明a比b大 , \比较器_3_上一位和当前位都相同 ,
       \比较器_3_说明a比b大 , \比较器_4_上一位和当前位都相同 , \比较器_4_说明a比b大 , \比较器_5_上一位和当前位都相同 , \比较器_5_说明a比b大 ,
       \比较器_6_上一位和当前位都相同 , \比较器_6_说明a比b大 , \比较器_7_上一位和当前位都相同 , \比较器_7_说明a比b大 ;

  \比较器  \u_比较器_1  (
    .A(A[7]), .B(B[7]), .\不相同 (\不相同的位数 [7]), .\上一个与门传下来的默认为1 (1'b1), .\上一位或门传下来的默认为0 (1'b0),
    .\上一位和当前位都相同 (\比较器_1_上一位和当前位都相同 ), .\说明A比B大 (\比较器_1_说明a比b大 ));
  \比较器  \u_比较器_2  (
    .A(A[6]), .B(B[6]), .\不相同 (\不相同的位数 [6]), .\上一个与门传下来的默认为1 (\比较器_1_上一位和当前位都相同 ),
    .\上一位或门传下来的默认为0 (\比较器_1_说明a比b大 ), .\上一位和当前位都相同 (\比较器_2_上一位和当前位都相同 ), .\说明A比B大 (\比较器_2_说明a比b大 ));
  \比较器  \u_比较器_3  (
    .A(A[5]), .B(B[5]), .\不相同 (\不相同的位数 [5]), .\上一个与门传下来的默认为1 (\比较器_2_上一位和当前位都相同 ),
    .\上一位或门传下来的默认为0 (\比较器_2_说明a比b大 ), .\上一位和当前位都相同 (\比较器_3_上一位和当前位都相同 ), .\说明A比B大 (\比较器_3_说明a比b大 ));
  \比较器  \u_比较器_4  (
    .A(A[4]), .B(B[4]), .\不相同 (\不相同的位数 [4]), .\上一个与门传下来的默认为1 (\比较器_3_上一位和当前位都相同 ),
    .\上一位或门传下来的默认为0 (\比较器_3_说明a比b大 ), .\上一位和当前位都相同 (\比较器_4_上一位和当前位都相同 ), .\说明A比B大 (\比较器_4_说明a比b大 ));
  \比较器  \u_比较器_5  (
    .A(A[3]), .B(B[3]), .\不相同 (\不相同的位数 [3]), .\上一个与门传下来的默认为1 (\比较器_4_上一位和当前位都相同 ),
    .\上一位或门传下来的默认为0 (\比较器_4_说明a比b大 ), .\上一位和当前位都相同 (\比较器_5_上一位和当前位都相同 ), .\说明A比B大 (\比较器_5_说明a比b大 ));
  \比较器  \u_比较器_6  (
    .A(A[2]), .B(B[2]), .\不相同 (\不相同的位数 [2]), .\上一个与门传下来的默认为1 (\比较器_5_上一位和当前位都相同 ),
    .\上一位或门传下来的默认为0 (\比较器_5_说明a比b大 ), .\上一位和当前位都相同 (\比较器_6_上一位和当前位都相同 ), .\说明A比B大 (\比较器_6_说明a比b大 ));
  \比较器  \u_比较器_7  (
    .A(A[1]), .B(B[1]), .\不相同 (\不相同的位数 [1]), .\上一个与门传下来的默认为1 (\比较器_6_上一位和当前位都相同 ),
    .\上一位或门传下来的默认为0 (\比较器_6_说明a比b大 ), .\上一位和当前位都相同 (\比较器_7_上一位和当前位都相同 ), .\说明A比B大 (\比较器_7_说明a比b大 ));
  \比较器  \u_比较器_8  (
    .A(A[0]), .B(B[0]), .\不相同 (\不相同的位数 [0]), .\上一个与门传下来的默认为1 (\比较器_7_上一位和当前位都相同 ),
    .\上一位或门传下来的默认为0 (\比较器_7_说明a比b大 ), .\上一位和当前位都相同 (\相同 ), .\说明A比B大 (\A大于B ));
endmodule

module \_38译码器  (
  input  A2,
  input  A1,
  input  A0,
  output Y0,
  output Y1,
  output Y2,
  output Y3,
  output Y4,
  output Y5,
  output Y6,
  output Y7
);

  wire not_1_out, not_2_out, not_3_out;

  not not_1 (not_1_out, A2);
  not not_2 (not_2_out, A1);
  not not_3 (not_3_out, A0);
  and and_1 (Y0, not_1_out, not_2_out, not_3_out);
  and and_2 (Y1, not_1_out, not_2_out, A0);
  and and_3 (Y2, not_1_out, A1, not_3_out);
  and and_4 (Y3, not_1_out, A1, A0);
  and and_5 (Y4, A2, not_2_out, not_3_out);
  and and_6 (Y5, A2, not_2_out, A0);
  and and_7 (Y6, A2, A1, not_3_out);
  and and_8 (Y7, A2, A1, A0);
endmodule

module ALU (
  input  shift_in___c_in,
  input  [7:0] A,
  input  [7:0] B,
  input  a_2,
  input  b_2,
  input  c,
  output \是否A大于B ,
  output \是否相同 ,
  output shift_out___c_out,
  output \是否为0 ,
  output [7:0] result
);

  wire \_38译码器_y0 , \_38译码器_y1 , \_38译码器_y2 , \_38译码器_y3 , \_38译码器_y4 , \_38译码器_y5 , \_38译码器_y6 , \加法_c_out ,
       \右移_shift_out , \左移_shift_out ;
  wire [7:0] \与_out , \加法_s , \右移_right_shift_out , \左移_left_shift_out , \或_out , \比较器_不相同的位数 , \非_out ;

  \_38译码器  \_38译码器  (
    .A2(a_2), .A1(b_2), .A0(c), .Y0(\_38译码器_y0 ), .Y1(\_38译码器_y1 ), .Y2(\_38译码器_y2 ), .Y3(\_38译码器_y3 ),
    .Y4(\_38译码器_y4 ), .Y5(\_38译码器_y5 ), .Y6(\_38译码器_y6 ));  // open: Y7
  \比较器8位  \u_比较器  (.A(A), .B(B), .\不相同的位数 (\比较器_不相同的位数 ), .\A大于B (\是否A大于B ), .\相同 (\是否相同 ));
  \与门8位  \u_与  (.A(A), .B(B), .OUT(\与_out ));
  \或门8位  \u_或  (.A(A), .B(B), .OUT(\或_out ));
  \非门8位  \u_非  (.IN(A), .OUT(\非_out ));
  \右移位器8位  \u_右移  (
    .right_shift_in(A), .shift_in(shift_in___c_in), .shift_out(\右移_shift_out ),
    .right_shift_out(\右移_right_shift_out ));
  \左移位器8位  \u_左移  (
    .shift_in(shift_in___c_in), .left_shift_in(A), .left_shift_out(\左移_left_shift_out ),
    .shift_out(\左移_shift_out ));
  \加法器8位  \u_加法  (.A(A), .C_IN(shift_in___c_in), .B(B), .S(\加法_s ), .C_OUT(\加法_c_out ));
  assign result = \_38译码器_y0  ? \比较器_不相同的位数  : 8'bz;  // Controlled_Buffer controlled_buffer_1
  assign result = \_38译码器_y1  ? \与_out  : 8'bz;  // Controlled_Buffer controlled_buffer_2
  assign result = \_38译码器_y2  ? \或_out  : 8'bz;  // Controlled_Buffer controlled_buffer_3
  assign result = \_38译码器_y3  ? \非_out  : 8'bz;  // Controlled_Buffer controlled_buffer_4
  assign result = \_38译码器_y4  ? \右移_right_shift_out  : 8'bz;  // Controlled_Buffer controlled_buffer_5
  assign shift_out___c_out = \_38译码器_y4  ? \右移_shift_out  : 1'bz;  // Controlled_Buffer controlled_buffer_6
  assign result = \_38译码器_y5  ? \左移_left_shift_out  : 8'bz;  // Controlled_Buffer controlled_buffer_7
  assign shift_out___c_out = \_38译码器_y5  ? \左移_shift_out  : 1'bz;  // Controlled_Buffer controlled_buffer_8
  assign result = \_38译码器_y6  ? \加法_s  : 8'bz;  // Controlled_Buffer controlled_buffer_9
  assign shift_out___c_out = \_38译码器_y6  ? \加法_c_out  : 1'bz;  // Controlled_Buffer controlled_buffer_10
  \判0  \u_判0  (.IN(result), .OUT(\是否为0 ));
endmodule

module \判0  (
  input  [7:0] IN,
  output OUT
);

  wire or_1_out;

  or or_1 (or_1_out, IN[0], IN[1], IN[2], IN[3], IN[4], IN[5], IN[6], IN[7]);
  not not_1 (OUT, or_1_out);
endmodule
